# Fritzing sketch plan (saved by Fritzing 0.8.7b)
breadboards: 1

parts:
  OLED_I2C1 = OLED 128x64 I2C Monochrome Display
  Mod1 = gy-906  # not connected
  Part1 = Arduino Nano (Rev3.0)
  S2 = Pushbutton [package="[THT]"]
  S3 = Toggle Switch [package=THT]
  Part2 = KY-006 Passive Buzzer Module [package="Breakout board"]  # not connected
  VCC1 = Battery block 9V
  R1 = Resistor [tolerance=±5% resistance=330 package=THT]

nets:
  N1: OLED_I2C1.SDA, Part1.A4
  N2: OLED_I2C1.SCK, Part1.A5
  N3: Part1.GND, S3.COM, VCC1.-
  N4: Part1.D2, S3.L1, R1.Pin_1
  N5: Part1.VIN, S2.Pin_3, S2.Pin_4
  N6: Part1.5V, R1.Pin_0
  N7: S2.Pin_1, S2.Pin_2, VCC1.+

custom parts:
  gy-906: gy-906 Non-contact PIR I2C interface temperature sensor breakout board.
  KY-006 Passive Buzzer Module: Passive Piezoelectric Buzzer Module Keyes KY-006, it can produce a range of sound tones depending on the input frequency.
  Battery block 9V: 9 Volt battery block with 200mil pcb footprint spacing and large connection pads
